# Fritzing sketch power cutter (saved by Fritzing 0.8.5b)
circuit board: 8.46667cm x 5.64444cm
breadboards: 1

parts:
  R1 = Resistor [tolerance=±5% resistance=2.2k package=THT]
  R2 = Resistor [tolerance=±5% resistance=2.2k package=THT]
  Q2 = npn-Powertransistor [part_number=BD139 package="TO220 [THT]"]
  RaspberryPi1 = Raspberry Pi Model B
  Q1 = NPN-Transistor [part_number=BC547 package="TO92 [THT]"]
  C1 = Ceramic Capacitor [capacitance=100nF package="100 mil [THT, multilayer]"]
  U2 = Voltage Regulator - 3.3V [part_number=LM7833 package="TO220 [THT]"]
  C2 = Ceramic Capacitor [capacitance=100nF package="100 mil [THT, multilayer]"]

nets:
  N1: R1.Pin_0, Q2.collector, RaspberryPi1.5V
  N2: R1.Pin_1, Q2.base, Q1.C
  N3: R2.Pin_0, RaspberryPi1.#18
  N4: R2.Pin_1, Q1.B
  N5: Q2.emitter, C1.1, U2.input_voltage
  GND: RaspberryPi1.GND, Q1.E, C1.0, U2.GND, C2.0
  +3.3V: U2.output_voltage, C2.1

custom parts:
  Raspberry Pi Model B: Raspberry Pi (Model B)
